# Fritzing sketch CumptichSenne_Fritzing_Breadboard (saved by Fritzing 0.9.4)
breadboards: 2

parts:
  Raspberry_Pi_1 = Raspberry Pi 4 [part_number=RPI-4-b]
  R1 = Resistor [tolerance=±5% resistance=4.7k package=THT]
  YwRobot_Power_Supply1 = YwRobot Breadboard Power Supply [part_number=545043]
  ADC1 = MCP3008 [package=dil16]
  DS1 = DS18B20 1-Wire Temperature Sensor [part_number=DS18B20]
  M1 = PH meter with sensor in breadboard [package=THT]
  U1 = LCD-16X2 [package=lcd-16x2_noholes]
  U2 = PCF8574 [package="DIP16 [THT]"]
  R2 = Trimmer Potentiometer [maximum_resistance=10kΩ package=THT]
  U3 = WS2812 RGB LED strip
  J1 = Buzzer
  M2 = IC, SIP package, 3 pins [chip_label="Kwaliteit meter"]

nets:
  N1: Raspberry_Pi_1.GPIO2, U2.SDA
  N2: Raspberry_Pi_1.GPIO3, U2.SCL
  VDD: Raspberry_Pi_1.GPIO4, R1.Pin_0, R1.Pin_1, YwRobot_Power_Supply1.VCC#5, ADC1.VREF, ADC1.VDD, DS1.DQ, DS1.VDD
  N3: Raspberry_Pi_1.GPIO10, ADC1.Din
  N4: Raspberry_Pi_1.GPIO9, ADC1.Dout
  N5: Raspberry_Pi_1.GPIO11, ADC1.CLK
  GND: Raspberry_Pi_1.GND, YwRobot_Power_Supply1.GND#11, DS1.GND, U1.VSS, U1.R_W, U2.A1, U2.A2, U2.GND, J1.pin1, M2.pin1
  N6: Raspberry_Pi_1.GPIO21, U1.RS
  N7: Raspberry_Pi_1.GPIO20, U1.E
  N8: Raspberry_Pi_1.GPIO16, J1.pin2
  N9: Raspberry_Pi_1.GPIO8, ADC1.CS/SHDN
  N10: Raspberry_Pi_1.GPIO18, U3.DIN
  VCC: YwRobot_Power_Supply1.VCC#9, M1.pin2, U1.VDD, U1.A, U2.VCC, R2.leg2, U3.VCC, M2.pin2
  N11: YwRobot_Power_Supply1.GND#13, ADC1.DGND, ADC1.AGND, M1.pin3, U1.K, R2.leg1, U3.GND
  N12: ADC1.CH0, M1.pin1
  N13: ADC1.CH1, M2.pin3
  N14: U1.VO, R2.wiper
  N15: U1.DB0, U2.P0
  N16: U1.DB1, U2.P1
  N17: U1.DB2, U2.P2
  N18: U1.DB3, U2.P3
  N19: U1.DB4, U2.P4
  N20: U1.DB5, U2.P5
  N21: U1.DB6, U2.P6
  N22: U1.DB7, U2.P7

custom parts:
  Raspberry Pi 4: The RPi4, a faster version of the awesome Raspberry Pi 2 B ARM Board with 40 pin gpio. Ready for special Raspberry Pi B+ and RPi2 Hat (Hardware attached (on) top)
  YwRobot Breadboard Power Supply: The YwRobot Breadboard Power Supply (MB-V2) has two power rails; they can be 5V or 3V3. Power to the module can be provided through the female USB socket or through the A10 (female) 2.1mm power jack.
  PH meter with sensor in breadboard: DFrobot PH meter (SKU SEN0161)
  WS2812 RGB LED strip: WS2812 strip
  Buzzer: Fixed frequency buzzer
